# Fritzing sketch Experience2 final (saved by Fritzing 0.9.2b)
breadboards: 1

parts:
  Composant1 = Arduino Uno (Rev3)
  R1 = Resistor [tolerance=±5% resistance=220 package=THT]
  L1 = Inductor [package="400 mil [THT]"]
  R2 = Resistor [tolerance=±5% resistance=220 package=THT]
  C1 = Capacitor [package=cap-pth-large]
  C2 = Capacitor [package=cap-pth-small2]
  D1 = Diode [package=diode-hv]
  R3 = Resistor [tolerance=±5% resistance=220 package=THT]
  LED1 = LED - 3mm [color="Red (633nm)" package="3 mm [THT]"]
  LED2 = LED - 3mm [color="Yellow (574nm)" package="3 mm [THT]"]
  LED3 = LED - 3mm [color="Blue (505nm)" package="3 mm [THT]"]
  R4 = Resistor [tolerance=±5% resistance=220 package=THT]
  R5 = Resistor [tolerance=±5% resistance=220 package=THT]
  R6 = Resistor [tolerance=±5% resistance=220 package=THT]

nets:
  N1: Composant1.A0, C2.2, D1.C, R3.Pin_0
  N2: Composant1.D9_PWM, R1.Pin_1
  GND: Composant1.GND, R2.Pin_1, C2.1, R3.Pin_1, LED1.cathode, LED2.cathode, LED3.cathode
  N3: Composant1.D2, R5.Pin_1
  N4: Composant1.D4, R4.Pin_1
  N5: Composant1.D7, R6.Pin_1
  N6: R1.Pin_0, L1.pin_0, R2.Pin_0
  N7: L1.pin_1, C1.2, D1.A
  Electrode: C1.1
  N8: LED1.anode, R4.Pin_0
  N9: LED2.anode, R5.Pin_0
  N10: LED3.anode, R6.Pin_0
